// Logisim project main.circ as structural Verilog: 4 circuits, main circuit main
module main (
  input  Reset
);

  wire decoder_1_out6, decoder_1_out7, LoadInstr;
  wire [2:0] rom_1_data;
  wire [4:0] addr, InstrAddr;

  instr_counter instr_counter_1 (.LoadAddress(LoadInstr), .AddressIn(addr), .reset(Reset), .AddressOut(InstrAddr));
  Decoder #(.select(3), .enable("false")) decoder_1 (
    .out6(decoder_1_out6), .out7(decoder_1_out7), .sel(rom_1_data));  // open: out0, out1, out2, out3, out4, out5
  or or_1 (LoadInstr, decoder_1_out7, decoder_1_out6);
  ROM #(.addrWidth(5)) rom_1 (.addr(InstrAddr), .data({rom_1_data, addr}), .sel(1'b1));
  RAM_module ram_module_1 ();  // open: DataIn, Address, MemWrite, Reset, DataOut

  // Other names for the same wires on the sheet: imm[3:0] = addr[3:0]; LoadAddr[4:0] = addr; offset[4:0] = addr;
  //   RFunc[2:0] = addr[2:0]; rx = addr[3]; rd = addr[4]
endmodule

// RAM
module RAM_module (
  input  [7:0] DataIn,
  input  [7:0] Address,
  input  Reset,
  input  MemWrite,
  output [7:0] DataOut
);

  wire clock_1_out, not_1_out;

  Clock clock_1 (.out(clock_1_out));
  not not_1 (not_1_out, MemWrite);
  assign DataOut = MemWrite ? DataIn : 8'bz;  // Controlled_Buffer controlled_buffer_1
  RAM ram_1 (.addr(Address), .data(DataOut), .sel(1'b1), .clk(clock_1_out), .ld(not_1_out), .clr(Reset));
endmodule

// IC
module instr_counter (
  input  LoadAddress,
  input  [4:0] AddressIn,
  input  reset,
  output [4:0] AddressOut
);

  wire clock_1_out, not_1_out;

  not not_1 (not_1_out, LoadAddress);
  Counter #(.width(5), .max('h1f), .ongoal("stay")) counter_1 (
    .load(LoadAddress), .D(AddressIn), .count(not_1_out), .Q(AddressOut), .clk(clock_1_out), .clr(reset));  // open: carry
  Clock clock_1 (.out(clock_1_out));
endmodule

module ALU (
  input  [7:0] rdInput,
  input  [7:0] rxInput,
  input  [2:0] func,
  input  en,
  output [7:0] Output
);

  wire [7:0] adder_1_out, and_1_out, negator_1_out, not_1_out, or_1_out, shifter_1_out, shifter_2_out,
       xor_1_out;

  assign or_1_out = rdInput | rxInput;  // OR_Gate or_1, 8 bits wide
  assign xor_1_out = rdInput ^ rxInput;  // XOR_Gate xor_1, 8 bits wide
  assign and_1_out = rdInput & rxInput;  // AND_Gate and_1, 8 bits wide
  Adder adder_1 (.a(rdInput), .b(rxInput), .out(adder_1_out), .cin(1'b0));  // open: cout
  Shifter #(.shift("lr")) shifter_1 (.in(rxInput), .\dist (3'b001), .out(shifter_1_out));
  Shifter #(.shift("ar")) shifter_2 (.in(rxInput), .\dist (3'b001), .out(shifter_2_out));
  assign not_1_out = ~rxInput;  // NOT_Gate not_1, 8 bits wide
  Negator negator_1 (.in(rxInput), .out(negator_1_out));
  Multiplexer #(.select(3), .width(8)) multiplexer_1 (
    .in0(or_1_out), .in1(xor_1_out), .in2(and_1_out), .in3(adder_1_out), .in4(shifter_1_out),
    .in5(shifter_2_out), .in6(not_1_out), .in7(negator_1_out), .out(Output), .sel(func), .en(en));
endmodule
